# Fritzing sketch Project_Galileo_Schema_Fritz (saved by Fritzing 0.9.4)
circuit board: 26.6978cm x 17.1712cm
breadboards: 1

parts:
  Part1 = Intel Galileo Gen2
  U1 = Vibration Motor- ROB-08449 [package=vibe-motor-10mm]
  DS2Y-5-DC5V1 = DS2Y-5-DC5V [part_number=DS2Y-5-DC5V]
  Water_Level_Sensor1 = Water Level Sensor
  Water_Level_Sensor2 = Water Level Sensor
  Water_Level_Sensor3 = Water Level Sensor
  Water_Level_Sensor4 = Water Level Sensor
  Water_Level_Sensor5 = Water Level Sensor
  Water_Level_Sensor6 = Water Level Sensor
  Water_Level_Sensor7 = Water Level Sensor
  Part2 = Standard LCD 16x2 white on blue [part_number=181]
  A1 = MH-FMD buzzer
  S1 = Pushbutton 6mm-6mm [package="[THT]"]
  R2 = Resistor [tolerance=±5% resistance=220 package=THT]
  R3 = Resistor [tolerance=±5% resistance=220 package=THT]

nets:
  N1: Part1.A0, Water_Level_Sensor6.SIG
  N2: Part1.A1, Water_Level_Sensor7.SIG
  N3: Part1.A2, Water_Level_Sensor5.SIG
  N4: Part1.A3, Water_Level_Sensor4.SIG
  N5: Part1.A4/SDA, Water_Level_Sensor3.SIG
  N6: Part1.A5/SCL, Water_Level_Sensor2.SIG
  N7: Part1.D9_PWM, Part2.DB4
  N8: Part1.D10_PWM/SS, Part2.DB5
  N9: Part1.D11_PWM/MOSI, Part2.DB6
  N10: Part1.D12/MISO, Part2.DB7
  GND: Part1.GND, DS2Y-5-DC5V1.16_-, Water_Level_Sensor1.GND, Water_Level_Sensor2.GND, Water_Level_Sensor3.GND, Water_Level_Sensor4.GND, Water_Level_Sensor5.GND, Water_Level_Sensor6.GND, Water_Level_Sensor7.GND, Part2.VSS, Part2.V0, Part2.R/W, Part2.LED-, A1.Pin_3, R3.Pin_1
  N11: Part1.D2, R2.Pin_0
  N12: Part1.D3_PWM, A1.Pin_2
  N13: Part1.D4, DS2Y-5-DC5V1.9_N.O.
  N14: Part1.D6_PWM, Water_Level_Sensor1.SIG
  N15: Part1.D7, Part2.RS
  VCC: Part1.5V, DS2Y-5-DC5V1.1_+, Water_Level_Sensor1.VCC, Water_Level_Sensor2.VCC, Water_Level_Sensor3.VCC, Water_Level_Sensor4.VCC, Water_Level_Sensor5.VCC, Water_Level_Sensor6.VCC, Water_Level_Sensor7.VCC, Part2.VDD, Part2.LED+, A1.Pin_1
  N16: U1.-, DS2Y-5-DC5V1.8_N.O.
  N17: S1.Pin_1, S1.Pin_2, R3.Pin_0
  N18: S1.Pin_3, S1.Pin_4, R2.Pin_1

custom parts:
  Water Level Sensor: A water level sensor. This sensor operates at 3V to 5V. The Sig (signal) pin outputs an analogue signal that is in proportion to the amount of water in contact with the sensor.
  Standard LCD 16x2 white on blue: Standard HD44780 LCDs are useful for creating standalone projects. * 16 characters wide, 2 rows * White text on blue background * Connection port is 0.1" pitch, single row for easy breadboarding and wiring
  MH-FMD buzzer: MH-FMD buzzer.
  Pushbutton 6mm-6mm: A generic pushbutton.

// code stored in the sketch: Untitled2.ino
#include <Wire.h>
#include <LiquidCrystal.h>
// declaration of components and association with the pins on the Galileo board
#define SENSOR1 A0 // defines the SENSOR1 water output port to the ANALOG port A0 in the board
#define SENSOR2 A1 // defines the SENSOR2 water output port to the ANALOG port A1 in the board
#define SENSOR3 A2 // defines the SENSOR3 water output port to the ANALOG port A2 in the board
#define SENSOR4 A3 // defines the SENSOR4 water output port to the ANALOG port A3 in the board
#define SENSOR5 A4 // defines the SENSOR5 water output port to the ANALOG port A4 in the board
#define SENSOR6 A5 // defines the SENSOR6 water output port to the ANALOG port A5 in the board
#define SENSOR7 6 // defines the output port of SENSOR7 water to digital port D6~ in the board

#define NUM_SENSORS 6
#define START_BUTTON 2 // define the digital PIN D2 of the board for START_BUTTON (Push Button)
#define BUZZER_PIN 3 // defines digital PIN D3 of the board for BUZZER_PIN
#define PUMP_RELAY 4 // defines the digital PIN D4 of the board for PUMP_RELAY

// initialize the library by associating any needed LCD interface pin with the galileo pin number it is connected to

const int rs = 7, en = 8, d4 = 9, d5 = 10, d6 = 11, d7 = 12;
LiquidCrystal lcd(rs, en, d4, d5, d6, d7);

void setup() { // loop to initialize setup;

 pinMode(START_BUTTON, INPUT_PULLUP); //declaring START_BUTTON pin as INPUT pin
 pinMode(PUMP_RELAY, OUTPUT); //declaring PUMP_RELAY pin as OUTPUT pin
 pinMode(BUZZER_PIN, OUTPUT); //declaring BUZZER_PIN pin as OUTPUT pin

 lcd.clear(); // Clears any text on the LCD display
 lcd.begin(16, 2); // 16 characters are displayed on 2 lines
 lcd.print("TANK:EMPTY"); // Display on the LCD screen the text: TANK:EMPTY
}

void loop() { // infinite execution loop START_BUTTON and Water Pump
 if (digitalRead(START_BUTTON) == LOW) { // Read the logic state of the digital input <Low=OFF>
 startPump(); // If the button is raised, an impulse is sent to the board
 } // and the pump start process begins
} // At the end of the loop() function, it resumes

void startPump() { // Process for starting the pump
 lcd.clear(); // Clears any text on the LCD display
 lcd.print("Water Pump: ON"); // Display the text on the LCD screen: "WATER PUMP: GOING"
 digitalWrite(PUMP_RELAY, HIGH); // setting PUMP_RELAY digital pin IN to HIGH=ON state

 int currentLevel = 0; // CurrentLevel is initialized with the value 0
 while (currentLevel < NUM_SENSORS) { // As long as it respects the condition " < "
 int sensorReading = analogRead(A0); //read the value on analog pin A0 from the Sensor

 int level = map(sensorReading, 0, 1023, 0, NUM_SENSORS);

 if (level > currentLevel) { // If the " > " condition is met
 currentLevel = level; // Then the level is the current level
 displayLevel(currentLevel); // The current level is displayed
 }

 delay(1000); // 1 sec delay (keep the state for another 1 second)
 }

 lcd.clear(); // Clears any text on the LCD display
 lcd.print("LEVEL: MAXIMUM"); // Display the text on the LCD screen: "PUMP RUNS"
 lcd.setCursor(0, 1); // It is set from which position the text should appear on the display
 lcd.print("PUMP: OFF"); // Display the text on the LCD screen: "WATER PUMP: OFF"
 digitalWrite(PUMP_RELAY, LOW); // setting PUMP_RELAY digital pin IN to LOW=OFF state

 activateBuzzer(); // Enable Buzzer
}

void displayLevel(int level) { // The level read by the sensor is displayed as level
 lcd.clear(); // Clears any text on the LCD display
 if (level == 0) { // If the read level = 0, then
 lcd.print("LEVEL: MINIMUM"); // Display the text on the LCD screen: "LEVEL: MINIMUM"
 } else if (level == NUM_SENSORS) { // Otherwise, if the level is equal to the one read by the sensors
 lcd.print("LEVEL: MAXIMUM"); // Then Display the text on the LCD screen: "LEVEL: MAXIMUM"
 } else { // Otherwise,
 lcd.print("Water Level: "); // Display the text on the LCD screen: "Water Level: "
 lcd.print(level); // Display level value
 }
 lcd.setCursor(0, 1); // It is set from which position the text should appear on the display
 lcd.print("PUMP: ON"); // Display the text on the LCD screen: "PUMP ON"
}

void activateBuzzer() { // START Buzzer
 digitalWrite(BUZZER_PIN, HIGH); // setting BUZZER_PIN digital pin IN to HIGH=ON state
 delay(100000); // Delay Buzz for 10 seconds
 digitalWrite(BUZZER_PIN, LOW); // setting BUZZER_PIN digital pin IN to LOW=OFF state
}
